# Fritzing sketch diagram (saved by Fritzing 0.9.10b)

parts:
  Part2 = Arduino Pro Mini v13
  microSD1 = MicroSD Card Module
  Part3 = Solid State High Level Relay Module [package=relay]
  Part4 = Passive Buzzer
  Part9 = FTDI Basic Programmer
  Grove1 = Grove 3 Axis Digital Accelerometer 16g
  J1 = female pin header, 2 pins [form="♀ (female)"]
  J2 = female pin header, 2 pins [form="♀ (female)"]
  J3 = female pin header, 2 pins [form="♀ (female)"]
  J4 = female pin header, 2 pins [form="♀ (female)"]

nets:
  N1: Part2.DTR, Part9.DTR
  N2: Part2.D0/TX, Part9.RXI
  N3: Part2.D1/RX, Part9.TXO
  N4: Part2.VCC, Part9.POWER
  GND: Part2.GND, Part9.GND
  N5: Part2.A4, Grove1.SDA
  N6: Part2.A5, Grove1.SCL
  N7: Part2.D13/SCK, microSD1.SCK
  N8: Part2.D12/MISO, microSD1.MISO
  N9: Part2.D11_PWM/MOSI, microSD1.MOSI
  N10: Part2.D10_PWM/SS, microSD1.CS
  N11: Part2.D9_PWM, Part4.S
  N12: Part2.D8, Part3.CH1
  N13: microSD1.GND, J1.pin1
  N14: microSD1.VCC, J1.pin2
  N15: Part3.DC+, J3.pin2
  N16: Part3.DC-, J3.pin1
  N17: Part4.GND, J4.pin2
  N18: Part4.NC, J4.pin1
  N19: Grove1.GND, J2.pin1
  N20: Grove1.VCC, J2.pin2

custom parts:
  Solid State High Level Relay Module: 5V Omron solid state relay 240V 2A output with resistance fuse.
